# Fritzing sketch plantronics (saved by Fritzing 0.9.9b)

parts:
  Part1 = Arduino Mega 2560 (Rev3)
  U1 = ESP8266 NodeMCU LoLin module
  Part2 = FC-28 Soil Hygrometer Module
  Part3 = FC-28 Soil Hygrometer Module - Probe
  Mod1 = KY-015 Temperature & Humidity Sensor Module [package="Breakout board"]
  Water_Level_Sensor1 = Water Level Sensor
  S1 = PH meter [package=THT]
  8_Channel_Relay1 = 8 Channel Power Relay

nets:
  N1: Part1.A0, Part2.AO
  N2: Part1.A1, Water_Level_Sensor1.SIG
  N3: Part1.A2, Mod1.S
  N4: Part1.A3, S1.pin1
  GND: Part1.GND, U1.GND, Part2.GND, Mod1.-, Water_Level_Sensor1.GND, S1.pin3, 8_Channel_Relay1.GND
  VCC: Part1.5V, Part2.VCC, Mod1.Vin, Water_Level_Sensor1.VCC, S1.pin2, 8_Channel_Relay1.VCC
  N5: Part1.D0_RX0, U1.TX
  N6: Part1.D1_TX0, U1.RX
  N7: Part1.D39, 8_Channel_Relay1.IN1
  N8: Part1.D41, 8_Channel_Relay1.IN2
  N9: Part1.D43, 8_Channel_Relay1.IN3
  N10: Part1.D45, 8_Channel_Relay1.IN4
  N11: Part1.D47, 8_Channel_Relay1.IN5
  N12: Part1.D49, 8_Channel_Relay1.IN6
  N13: Part1.D51, 8_Channel_Relay1.IN7
  N14: Part1.D53, 8_Channel_Relay1.IN8
  N15: Part2.POS, Part3.POS
  N16: Part2.NEG, Part3.NEG

custom parts:
  ESP8266 NodeMCU LoLin module: ESP8266 based NodeMCU
  FC-28 Soil Hygrometer Module: The FC-28 is a soil hygrometer module that uses the Texas Instruments LM393 comparator chip to provide an analog measurement of soil humidity. The digital output is high when soil moisture is over a certain threshold, as determined by adjusting the potentiometer.
  FC-28 Soil Hygrometer Module - Probe: The FC-28 is a soil hygrometer module that uses the Texas Instruments LM393 comparator chip to provide an analog measurement of soil humidity.
  KY-015 Temperature & Humidity Sensor Module: KY-015 temperature and humidity sensor module, provides a low-latency serial interface to measure humidity and temperature.
  Water Level Sensor: A water level sensor. This sensor operates at 3V to 5V. The Sig (signal) pin outputs an analogue signal that is in proportion to the amount of water in contact with the sensor.
  8 Channel Power Relay: An 8 channel power relay. The module operates at 5V.
